// Logisim project enigma.circ as structural Verilog: 10 circuits, main circuit main
module main (
);

  wire A_out, B_out, C_out, connector_in_1_out_11, connector_in_1_out_12, connector_in_1_out_13,
       connector_in_1_out_14, connector_in_1_out_15, connector_in_1_out_16, connector_in_1_out_17,
       connector_in_1_out_18, connector_in_1_out_19, connector_in_2_out_11, connector_in_2_out_12,
       connector_in_2_out_13, connector_in_2_out_14, connector_in_2_out_15, connector_in_2_out_16,
       connector_in_2_out_17, connector_in_2_out_18, connector_in_3_out_11, connector_in_3_out_12,
       connector_in_3_out_13, connector_in_3_out_14, connector_in_3_out_15, connector_in_3_out_16,
       connector_in_3_out_17, connector_in_3_out_18, connector_in_3_out_19, D_out, E_out, F_out, G_out,
       H_out, I_out, J_out, K_out, L_out, letter_converter_1_out_28, letter_converter_1_out_29,
       letter_converter_1_out_30, letter_converter_1_out_31, letter_converter_1_out_33,
       letter_converter_1_out_34, letter_converter_1_out_35, letter_converter_1_out_37,
       letter_converter_1_out_38, letter_converter_1_out_39, letter_converter_1_out_40,
       letter_converter_1_out_41, letter_converter_1_out_43, letter_converter_1_out_46,
       letter_converter_1_out_49, letter_converter_1_out_51, letter_converter_1_out_52,
       letter_converter_2_out_29, letter_converter_2_out_30, letter_converter_2_out_32,
       letter_converter_2_out_36, letter_converter_2_out_39, letter_converter_2_out_40,
       letter_converter_2_out_41, letter_converter_2_out_42, letter_converter_2_out_43,
       letter_converter_2_out_44, letter_converter_2_out_45, letter_converter_2_out_47,
       letter_converter_2_out_48, letter_converter_2_out_49, letter_converter_2_out_50,
       letter_converter_2_out_51, letter_converter_2_out_52, letter_converter_2_out_53,
       letter_converter_3_out_28, letter_converter_3_out_31, letter_converter_3_out_32,
       letter_converter_3_out_33, letter_converter_3_out_34, letter_converter_3_out_35,
       letter_converter_3_out_36, letter_converter_3_out_37, letter_converter_3_out_38,
       letter_converter_3_out_42, letter_converter_3_out_44, letter_converter_3_out_45,
       letter_converter_3_out_46, letter_converter_3_out_47, letter_converter_3_out_48,
       letter_converter_3_out_50, letter_converter_3_out_53, M_out, N_out, O_out, out_1_out_2, out_1_out_3,
       out_1_out_4, out_1_out_5, out_1_out_6, out_1_out_7, out_1_out_8, out_1_out_9, out_1_out_10,
       out_2_out_2, out_2_out_3, out_2_out_4, out_2_out_5, out_2_out_6, out_2_out_7, out_2_out_8,
       out_2_out_9, out_3_out_2, out_3_out_3, out_3_out_4, out_3_out_5, out_3_out_6, out_3_out_7,
       out_3_out_8, out_3_out_9, out_3_out_10, P_out, Q_out, R_out, S_out, switch_1_out_3, switch_1_out_4,
       switch_2_out_3, switch_2_out_4, switch_3_out_3, switch_3_out_4, switch_4_out_3, switch_4_out_4,
       switch_5_out_3, switch_5_out_4, switch_6_out_3, switch_6_out_4, switch_7_out_3, switch_7_out_4,
       switch_8_out_3, switch_8_out_4, switch_9_out_3, switch_9_out_4, switch_10_out_3, switch_10_out_4,
       switch_11_out_3, switch_11_out_4, switch_12_out_3, switch_12_out_4, switch_13_out_3, switch_13_out_4,
       switch_14_out_3, switch_14_out_4, switch_15_out_3, switch_15_out_4, switch_16_out_3, switch_16_out_4,
       switch_17_out_3, switch_17_out_4, switch_18_out_3, switch_18_out_4, switch_19_out_3, switch_19_out_4,
       switch_20_out_3, switch_20_out_4, switch_21_out_3, switch_21_out_4, switch_22_out_3, switch_22_out_4,
       switch_23_out_3, switch_23_out_4, switch_24_out_3, switch_24_out_4, switch_25_out_3, switch_25_out_4,
       switch_26_out_3, switch_26_out_4, T_out, U_out, undriven, undriven_2, undriven_3, undriven_4,
       undriven_5, undriven_6, undriven_7, undriven_8, undriven_9, undriven_10, undriven_11, undriven_12,
       undriven_13, undriven_14, undriven_15, undriven_16, undriven_17, undriven_18, undriven_19,
       undriven_20, undriven_21, undriven_22, undriven_23, undriven_24, undriven_25, undriven_26,
       undriven_27, undriven_28, undriven_29, undriven_30, undriven_31, undriven_32, undriven_33,
       undriven_34, undriven_35, undriven_36, undriven_37, undriven_38, undriven_39, undriven_40,
       undriven_41, undriven_42, undriven_43, undriven_44, undriven_45, undriven_46, undriven_47,
       undriven_48, undriven_49, undriven_50, undriven_51, undriven_52, V_out, W_out, X_out, Y_out, Z_out;
  wire [8:0] connector_in_1_out_20, connector_in_2_out_20, connector_in_3_out_20, connector_in_4_out_20,
       connector_in_5_out_20, connector_in_6_out_20, letter_converter_1_out_44, letter_converter_2_out_28,
       letter_converter_3_out_43;
  wire [25:6] letter_converter_1_out_54;

  switch switch_1 (.in_1(Q_out), .in_2(connector_in_1_out_11), .out_3(switch_1_out_3), .out_4(switch_1_out_4));
  Button Q (.out(Q_out));
  connector_in connector_in_1 (
    .in_1(switch_1_out_4), .in_2(switch_4_out_4), .in_3(switch_5_out_4), .in_4(switch_11_out_4),
    .out_20(connector_in_1_out_20), .in_5(switch_10_out_4), .in_6(switch_17_out_4), .in_7(switch_16_out_4),
    .in_8(switch_23_out_4), .in_9(switch_22_out_4), .out_11(connector_in_1_out_11),
    .out_12(connector_in_1_out_12), .out_13(connector_in_1_out_13), .out_14(connector_in_1_out_14),
    .out_15(connector_in_1_out_15), .out_16(connector_in_1_out_16), .out_17(connector_in_1_out_17),
    .out_18(connector_in_1_out_18), .out_19(connector_in_1_out_19), .in_10(letter_converter_1_out_44));
  Button A (.out(A_out));
  switch switch_2 (.in_1(A_out), .in_2(connector_in_2_out_11), .out_3(switch_2_out_3), .out_4(switch_2_out_4));
  connector_in connector_in_2 (
    .in_1(switch_2_out_4), .in_2(switch_6_out_4), .in_3(switch_7_out_4), .in_4(switch_12_out_4),
    .out_20(connector_in_2_out_20), .in_5(switch_13_out_4), .in_6(switch_18_out_4), .in_7(switch_19_out_4),
    .in_8(switch_24_out_4), .out_11(connector_in_2_out_11), .out_12(connector_in_2_out_12),
    .out_13(connector_in_2_out_13), .out_14(connector_in_2_out_14), .out_15(connector_in_2_out_15),
    .out_16(connector_in_2_out_16), .out_17(connector_in_2_out_17), .out_18(connector_in_2_out_18),
    .in_10(letter_converter_2_out_28));  // open: in_9, out_19
  Button P (.out(P_out));
  switch switch_3 (.in_1(P_out), .in_2(connector_in_3_out_11), .out_3(switch_3_out_3), .out_4(switch_3_out_4));
  connector_in connector_in_3 (
    .in_1(switch_3_out_4), .in_2(switch_8_out_4), .in_3(switch_9_out_4), .in_4(switch_15_out_4),
    .out_20(connector_in_3_out_20), .in_5(switch_14_out_4), .in_6(switch_21_out_4), .in_7(switch_20_out_4),
    .in_8(switch_25_out_4), .in_9(switch_26_out_4), .out_11(connector_in_3_out_11),
    .out_12(connector_in_3_out_12), .out_13(connector_in_3_out_13), .out_14(connector_in_3_out_14),
    .out_15(connector_in_3_out_15), .out_16(connector_in_3_out_16), .out_17(connector_in_3_out_17),
    .out_18(connector_in_3_out_18), .out_19(connector_in_3_out_19), .in_10(letter_converter_3_out_43));
  switch switch_4 (.in_1(W_out), .in_2(connector_in_1_out_12), .out_3(switch_4_out_3), .out_4(switch_4_out_4));
  Button W (.out(W_out));
  switch switch_5 (.in_1(E_out), .in_2(connector_in_1_out_13), .out_3(switch_5_out_3), .out_4(switch_5_out_4));
  Button E (.out(E_out));
  Button D (.out(D_out));
  switch switch_6 (.in_1(S_out), .in_2(connector_in_2_out_12), .out_3(switch_6_out_3), .out_4(switch_6_out_4));
  Button S (.out(S_out));
  switch switch_7 (.in_1(D_out), .in_2(connector_in_2_out_13), .out_3(switch_7_out_3), .out_4(switch_7_out_4));
  switch switch_8 (.in_1(Y_out), .in_2(connector_in_3_out_12), .out_3(switch_8_out_3), .out_4(switch_8_out_4));
  switch switch_9 (.in_1(X_out), .in_2(connector_in_3_out_13), .out_3(switch_9_out_3), .out_4(switch_9_out_4));
  Button Y (.out(Y_out));
  Button X (.out(X_out));
  switch switch_10 (.in_1(T_out), .in_2(connector_in_1_out_15), .out_3(switch_10_out_3), .out_4(switch_10_out_4));
  switch switch_11 (.in_1(R_out), .in_2(connector_in_1_out_14), .out_3(switch_11_out_3), .out_4(switch_11_out_4));
  Button T (.out(T_out));
  Button R (.out(R_out));
  switch switch_12 (.in_1(F_out), .in_2(connector_in_2_out_14), .out_3(switch_12_out_3), .out_4(switch_12_out_4));
  Button F (.out(F_out));
  switch switch_13 (.in_1(G_out), .in_2(connector_in_2_out_15), .out_3(switch_13_out_3), .out_4(switch_13_out_4));
  Button G (.out(G_out));
  switch switch_14 (.in_1(V_out), .in_2(connector_in_3_out_15), .out_3(switch_14_out_3), .out_4(switch_14_out_4));
  Button C (.out(C_out));
  switch switch_15 (.in_1(C_out), .in_2(connector_in_3_out_14), .out_3(switch_15_out_3), .out_4(switch_15_out_4));
  Button V (.out(V_out));
  switch switch_16 (.in_1(U_out), .in_2(connector_in_1_out_17), .out_3(switch_16_out_3), .out_4(switch_16_out_4));
  Button Z (.out(Z_out));
  switch switch_17 (.in_1(Z_out), .in_2(connector_in_1_out_16), .out_3(switch_17_out_3), .out_4(switch_17_out_4));
  Button U (.out(U_out));
  Button H (.out(H_out));
  Button J (.out(J_out));
  switch switch_18 (.in_1(H_out), .in_2(connector_in_2_out_16), .out_3(switch_18_out_3), .out_4(switch_18_out_4));
  switch switch_19 (.in_1(J_out), .in_2(connector_in_2_out_17), .out_3(switch_19_out_3), .out_4(switch_19_out_4));
  switch switch_20 (.in_1(N_out), .in_2(connector_in_3_out_17), .out_3(switch_20_out_3), .out_4(switch_20_out_4));
  switch switch_21 (.in_1(B_out), .in_2(connector_in_3_out_16), .out_3(switch_21_out_3), .out_4(switch_21_out_4));
  Button B (.out(B_out));
  Button N (.out(N_out));
  connector_in connector_in_4 (
    .in_1(switch_22_out_3), .in_2(switch_23_out_3), .in_3(switch_16_out_3), .in_4(switch_17_out_3),
    .out_20(connector_in_4_out_20), .in_5(switch_10_out_3), .in_6(switch_11_out_3), .in_7(switch_5_out_3),
    .in_8(switch_4_out_3), .in_9(switch_1_out_3));  // open: out_11, out_12, out_13, out_14, out_15, out_16, out_17, out_18, out_19, in_10
  switch switch_22 (.in_1(O_out), .in_2(connector_in_1_out_19), .out_3(switch_22_out_3), .out_4(switch_22_out_4));
  Button O (.out(O_out));
  Button I (.out(I_out));
  switch switch_23 (.in_1(I_out), .in_2(connector_in_1_out_18), .out_3(switch_23_out_3), .out_4(switch_23_out_4));
  letter_converter letter_converter_1 (
    .in_1(undriven_51), .in_2(undriven_50), .in_3(undriven_47), .in_4(undriven_44),
    .in_5(connector_in_1_out_20[2]), .in_6(undriven_40), .in_7(undriven_38), .in_8(undriven_36),
    .in_9(connector_in_1_out_20[7]), .in_10(undriven_32), .in_11(undriven_31), .in_12(undriven_30),
    .in_13(undriven_28), .in_14(undriven_25), .in_15(connector_in_1_out_20[8]), .in_16(undriven_21),
    .in_17(connector_in_1_out_20[0]), .in_18(connector_in_1_out_20[3]), .in_19(undriven_14),
    .in_20(connector_in_1_out_20[4]), .in_21(connector_in_1_out_20[6]), .in_22(undriven_9),
    .in_23(connector_in_1_out_20[1]), .in_24(undriven_6), .in_25(undriven_3),
    .in_26(connector_in_1_out_20[5]),
    .out_54({letter_converter_1_out_54[23], letter_converter_1_out_54[21], letter_converter_1_out_54[25:24], letter_converter_1_out_54[18], letter_converter_1_out_54[23], letter_converter_1_out_54[6], letter_converter_1_out_54[16], {2{letter_converter_1_out_54[19]}}, letter_converter_1_out_54[16], letter_converter_1_out_54[12], letter_converter_1_out_54[21], letter_converter_1_out_54[8:7], letter_converter_1_out_54[25], letter_converter_1_out_54[14], letter_converter_1_out_54[11], letter_converter_1_out_54[24], letter_converter_1_out_54[14], letter_converter_1_out_54[11], letter_converter_1_out_54[7], letter_converter_1_out_54[12], letter_converter_1_out_54[6], letter_converter_1_out_54[18], letter_converter_1_out_54[8]}),
    .out_28(letter_converter_1_out_28), .out_29(letter_converter_1_out_29),
    .out_30(letter_converter_1_out_30), .out_31(letter_converter_1_out_31),
    .out_32(letter_converter_1_out_44[2]), .out_33(letter_converter_1_out_33),
    .out_34(letter_converter_1_out_34), .out_35(letter_converter_1_out_35),
    .out_36(letter_converter_1_out_44[7]), .out_37(letter_converter_1_out_37),
    .out_38(letter_converter_1_out_38), .out_39(letter_converter_1_out_39),
    .out_40(letter_converter_1_out_40), .out_41(letter_converter_1_out_41),
    .out_42(letter_converter_1_out_44[8]), .out_43(letter_converter_1_out_43),
    .out_44(letter_converter_1_out_44[0]), .out_45(letter_converter_1_out_44[3]),
    .out_46(letter_converter_1_out_46), .out_47(letter_converter_1_out_44[4]),
    .out_48(letter_converter_1_out_44[6]), .out_49(letter_converter_1_out_49),
    .out_50(letter_converter_1_out_44[1]), .out_51(letter_converter_1_out_51),
    .out_52(letter_converter_1_out_52), .out_53(letter_converter_1_out_44[5]),
    .in_27({letter_converter_1_out_54[23], letter_converter_1_out_54[21], letter_converter_1_out_54[25:24], letter_converter_1_out_54[18], letter_converter_1_out_54[23], letter_converter_1_out_54[6], letter_converter_1_out_54[16], {2{letter_converter_1_out_54[19]}}, letter_converter_1_out_54[16], letter_converter_1_out_54[12], letter_converter_1_out_54[21], letter_converter_1_out_54[8:7], letter_converter_1_out_54[25], letter_converter_1_out_54[14], letter_converter_1_out_54[11], letter_converter_1_out_54[24], letter_converter_1_out_54[14], letter_converter_1_out_54[11], letter_converter_1_out_54[7], letter_converter_1_out_54[12], letter_converter_1_out_54[6], letter_converter_1_out_54[18], letter_converter_1_out_54[8]}));
  switch switch_24 (.in_1(K_out), .in_2(connector_in_2_out_18), .out_3(switch_24_out_3), .out_4(switch_24_out_4));
  Button K (.out(K_out));
  letter_converter letter_converter_2 (
    .in_1(connector_in_2_out_20[0]), .in_2(undriven_48), .in_3(undriven_45), .in_4(connector_in_2_out_20[2]),
    .in_5(undriven_41), .in_6(connector_in_2_out_20[3]), .in_7(connector_in_2_out_20[4]),
    .in_8(connector_in_2_out_20[5]), .in_9(undriven_33), .in_10(connector_in_2_out_20[6]),
    .in_11(connector_in_2_out_20[7]), .in_12(undriven_29), .in_13(undriven_26), .in_14(undriven_24),
    .in_15(undriven_22), .in_16(undriven_19), .in_17(undriven_17), .in_18(undriven_15),
    .in_19(connector_in_2_out_20[1]), .in_20(undriven_12), .in_21(undriven_10), .in_22(undriven_8),
    .in_23(undriven_7), .in_24(undriven_4), .in_25(undriven_2), .in_26(undriven),
    .out_54({letter_converter_1_out_54[23], letter_converter_1_out_54[21], letter_converter_1_out_54[25:24], letter_converter_1_out_54[18], letter_converter_1_out_54[23], letter_converter_1_out_54[6], letter_converter_1_out_54[16], {2{letter_converter_1_out_54[19]}}, letter_converter_1_out_54[16], letter_converter_1_out_54[12], letter_converter_1_out_54[21], letter_converter_1_out_54[8:7], letter_converter_1_out_54[25], letter_converter_1_out_54[14], letter_converter_1_out_54[11], letter_converter_1_out_54[24], letter_converter_1_out_54[14], letter_converter_1_out_54[11], letter_converter_1_out_54[7], letter_converter_1_out_54[12], letter_converter_1_out_54[6], letter_converter_1_out_54[18], letter_converter_1_out_54[8]}),
    .out_28(letter_converter_2_out_28[0]), .out_29(letter_converter_2_out_29),
    .out_30(letter_converter_2_out_30), .out_31(letter_converter_2_out_28[2]),
    .out_32(letter_converter_2_out_32), .out_33(letter_converter_2_out_28[3]),
    .out_34(letter_converter_2_out_28[4]), .out_35(letter_converter_2_out_28[5]),
    .out_36(letter_converter_2_out_36), .out_37(letter_converter_2_out_28[6]),
    .out_38(letter_converter_2_out_28[7]), .out_39(letter_converter_2_out_39),
    .out_40(letter_converter_2_out_40), .out_41(letter_converter_2_out_41),
    .out_42(letter_converter_2_out_42), .out_43(letter_converter_2_out_43),
    .out_44(letter_converter_2_out_44), .out_45(letter_converter_2_out_45),
    .out_46(letter_converter_2_out_28[1]), .out_47(letter_converter_2_out_47),
    .out_48(letter_converter_2_out_48), .out_49(letter_converter_2_out_49),
    .out_50(letter_converter_2_out_50), .out_51(letter_converter_2_out_51),
    .out_52(letter_converter_2_out_52), .out_53(letter_converter_2_out_53),
    .in_27({letter_converter_1_out_54[23], letter_converter_1_out_54[21], letter_converter_1_out_54[25:24], letter_converter_1_out_54[18], letter_converter_1_out_54[23], letter_converter_1_out_54[6], letter_converter_1_out_54[16], {2{letter_converter_1_out_54[19]}}, letter_converter_1_out_54[16], letter_converter_1_out_54[12], letter_converter_1_out_54[21], letter_converter_1_out_54[8:7], letter_converter_1_out_54[25], letter_converter_1_out_54[14], letter_converter_1_out_54[11], letter_converter_1_out_54[24], letter_converter_1_out_54[14], letter_converter_1_out_54[11], letter_converter_1_out_54[7], letter_converter_1_out_54[12], letter_converter_1_out_54[6], letter_converter_1_out_54[18], letter_converter_1_out_54[8]}));
  connector_in connector_in_5 (
    .in_1(switch_26_out_3), .in_2(switch_25_out_3), .in_3(switch_20_out_3), .in_4(switch_21_out_3),
    .out_20(connector_in_5_out_20), .in_5(switch_14_out_3), .in_6(switch_15_out_3), .in_7(switch_9_out_3),
    .in_8(switch_8_out_3), .in_9(switch_3_out_3));  // open: out_11, out_12, out_13, out_14, out_15, out_16, out_17, out_18, out_19, in_10
  Button M (.out(M_out));
  switch switch_25 (.in_1(M_out), .in_2(connector_in_3_out_18), .out_3(switch_25_out_3), .out_4(switch_25_out_4));
  switch switch_26 (.in_1(L_out), .in_2(connector_in_3_out_19), .out_3(switch_26_out_3), .out_4(switch_26_out_4));
  Button L (.out(L_out));
  letter_converter letter_converter_3 (
    .in_1(undriven_52), .in_2(connector_in_3_out_20[5]), .in_3(connector_in_3_out_20[3]), .in_4(undriven_49),
    .in_5(undriven_46), .in_6(undriven_43), .in_7(undriven_42), .in_8(undriven_39), .in_9(undriven_37),
    .in_10(undriven_35), .in_11(undriven_34), .in_12(connector_in_3_out_20[8]),
    .in_13(connector_in_3_out_20[7]), .in_14(connector_in_3_out_20[6]), .in_15(undriven_27),
    .in_16(connector_in_3_out_20[0]), .in_17(undriven_23), .in_18(undriven_20), .in_19(undriven_18),
    .in_20(undriven_16), .in_21(undriven_13), .in_22(connector_in_3_out_20[4]), .in_23(undriven_11),
    .in_24(connector_in_3_out_20[2]), .in_25(connector_in_3_out_20[1]), .in_26(undriven_5),
    .out_54({letter_converter_1_out_54[23], letter_converter_1_out_54[21], letter_converter_1_out_54[25:24], letter_converter_1_out_54[18], letter_converter_1_out_54[23], letter_converter_1_out_54[6], letter_converter_1_out_54[16], {2{letter_converter_1_out_54[19]}}, letter_converter_1_out_54[16], letter_converter_1_out_54[12], letter_converter_1_out_54[21], letter_converter_1_out_54[8:7], letter_converter_1_out_54[25], letter_converter_1_out_54[14], letter_converter_1_out_54[11], letter_converter_1_out_54[24], letter_converter_1_out_54[14], letter_converter_1_out_54[11], letter_converter_1_out_54[7], letter_converter_1_out_54[12], letter_converter_1_out_54[6], letter_converter_1_out_54[18], letter_converter_1_out_54[8]}),
    .out_28(letter_converter_3_out_28), .out_29(letter_converter_3_out_43[5]),
    .out_30(letter_converter_3_out_43[3]), .out_31(letter_converter_3_out_31),
    .out_32(letter_converter_3_out_32), .out_33(letter_converter_3_out_33),
    .out_34(letter_converter_3_out_34), .out_35(letter_converter_3_out_35),
    .out_36(letter_converter_3_out_36), .out_37(letter_converter_3_out_37),
    .out_38(letter_converter_3_out_38), .out_39(letter_converter_3_out_43[8]),
    .out_40(letter_converter_3_out_43[7]), .out_41(letter_converter_3_out_43[6]),
    .out_42(letter_converter_3_out_42), .out_43(letter_converter_3_out_43[0]),
    .out_44(letter_converter_3_out_44), .out_45(letter_converter_3_out_45),
    .out_46(letter_converter_3_out_46), .out_47(letter_converter_3_out_47),
    .out_48(letter_converter_3_out_48), .out_49(letter_converter_3_out_43[4]),
    .out_50(letter_converter_3_out_50), .out_51(letter_converter_3_out_43[2]),
    .out_52(letter_converter_3_out_43[1]), .out_53(letter_converter_3_out_53),
    .in_27({letter_converter_1_out_54[23], letter_converter_1_out_54[21], letter_converter_1_out_54[25:24], letter_converter_1_out_54[18], letter_converter_1_out_54[23], letter_converter_1_out_54[6], letter_converter_1_out_54[16], {2{letter_converter_1_out_54[19]}}, letter_converter_1_out_54[16], letter_converter_1_out_54[12], letter_converter_1_out_54[21], letter_converter_1_out_54[8:7], letter_converter_1_out_54[25], letter_converter_1_out_54[14], letter_converter_1_out_54[11], letter_converter_1_out_54[24], letter_converter_1_out_54[14], letter_converter_1_out_54[11], letter_converter_1_out_54[7], letter_converter_1_out_54[12], letter_converter_1_out_54[6], letter_converter_1_out_54[18], letter_converter_1_out_54[8]}));
  connector_in connector_in_6 (
    .in_2(switch_24_out_3), .in_3(switch_19_out_3), .in_4(switch_18_out_3), .out_20(connector_in_6_out_20),
    .in_5(switch_13_out_3), .in_6(switch_12_out_3), .in_7(switch_7_out_3), .in_8(switch_6_out_3),
    .in_9(switch_2_out_3));  // open: in_1, out_11, out_12, out_13, out_14, out_15, out_16, out_17, out_18, out_19, in_10
  connector_out out_1 (
    .out_2(out_1_out_2), .out_3(out_1_out_3), .out_4(out_1_out_4), .out_5(out_1_out_5), .out_6(out_1_out_6),
    .out_7(out_1_out_7), .out_8(out_1_out_8), .out_9(out_1_out_9), .out_10(out_1_out_10),
    .in_1(connector_in_4_out_20));
  LED W_2 (.in(out_1_out_3));
  LED Q_2 (.in(out_1_out_2));
  connector_out out_2 (
    .out_2(out_2_out_2), .out_3(out_2_out_3), .out_4(out_2_out_4), .out_5(out_2_out_5), .out_6(out_2_out_6),
    .out_7(out_2_out_7), .out_8(out_2_out_8), .out_9(out_2_out_9), .in_1(connector_in_6_out_20));  // open: out_10
  LED A_2 (.in(out_2_out_2));
  LED S_2 (.in(out_2_out_3));
  connector_out out_3 (
    .out_2(out_3_out_2), .out_3(out_3_out_3), .out_4(out_3_out_4), .out_5(out_3_out_5), .out_6(out_3_out_6),
    .out_7(out_3_out_7), .out_8(out_3_out_8), .out_9(out_3_out_9), .out_10(out_3_out_10),
    .in_1(connector_in_5_out_20));
  LED P_2 (.in(out_3_out_2));
  LED Y_2 (.in(out_3_out_3));
  LED X_2 (.in(out_3_out_4));
  LED R_2 (.in(out_1_out_5));
  LED T_2 (.in(out_1_out_6));
  LED E_2 (.in(out_1_out_4));
  LED F_2 (.in(out_2_out_5));
  LED G_2 (.in(out_2_out_6));
  LED D_2 (.in(out_2_out_4));
  LED C_2 (.in(out_3_out_5));
  LED V_2 (.in(out_3_out_6));
  LED I_2 (.in(out_1_out_9));
  LED U_2 (.in(out_1_out_8));
  LED Z_2 (.in(out_1_out_7));
  LED H_2 (.in(out_2_out_7));
  LED J_2 (.in(out_2_out_8));
  LED B_2 (.in(out_3_out_7));
  LED M_2 (.in(out_3_out_9));
  LED N_2 (.in(out_3_out_8));
  LED O_2 (.in(out_1_out_10));
  LED K_2 (.in(out_2_out_9));
  LED L_2 (.in(out_3_out_10));

  // Notes on the sheet:
  //   Plugboard
  //   Reflector
endmodule

module rotor (
  input  [25:0] in_1,
  output [25:0] out_2,
  output [4:0] out_3
);

  wire clock_1_out;
  wire [4:0] adder_1_out, counter_1_q, encoder_1_out_2;

  // Probe on encoder_1_out_2
  encoder encoder_1 (.in_1(in_1), .out_2(encoder_1_out_2));
  Counter #(.width(5), .max('h19)) counter_1 (.Q(counter_1_q), .clk(clock_1_out));  // open: load, D, count, carry, clr
  Clock clock_1 (.out(clock_1_out));
  Demultiplexer #(.select(5)) demultiplexer_1 (
    .out0(out_2[0]), .out1(out_2[1]), .out2(out_2[2]), .out3(out_2[3]), .out4(out_2[4]), .out5(out_2[5]),
    .out6(out_2[6]), .out7(out_2[7]), .out8(out_2[8]), .out9(out_2[9]), .out10(out_2[10]), .out11(out_2[11]),
    .out12(out_2[12]), .out13(out_2[13]), .out14(out_2[14]), .out15(out_2[15]), .out16(out_2[16]),
    .out17(out_2[17]), .out18(out_2[18]), .out19(out_2[19]), .out20(out_2[20]), .out21(out_2[21]),
    .out22(out_2[22]), .out23(out_2[23]), .out24(out_2[24]), .out25(out_2[25]), .in(1'b1), .sel(adder_1_out),
    .en(1'b1));  // open: out26, out27, out28, out29, out30, out31
  // Probe on adder_1_out
  Adder #(.width(5)) adder_1 (.a(encoder_1_out_2), .b(counter_1_q), .out(adder_1_out));  // open: cin, cout
  // Probe on out_2
  encoder encoder_2 (.in_1(out_2), .out_2(out_3));
endmodule

module encoder (
  input  [25:0] in_1,
  output [4:0] out_2
);

  wire priority_encoder_1_en_out, priority_encoder_1_gs;

  // Probe on out_2
  Priority_Encoder #(.select(5)) priority_encoder_1 (
    .in0(in_1[0]), .in1(in_1[1]), .in2(in_1[2]), .in3(in_1[3]), .in4(in_1[4]), .in5(in_1[5]), .in6(in_1[6]),
    .in7(in_1[7]), .in8(in_1[8]), .in9(in_1[9]), .in10(in_1[10]), .in11(in_1[11]), .in12(in_1[12]),
    .in13(in_1[13]), .in14(in_1[14]), .in15(in_1[15]), .in16(in_1[16]), .in17(in_1[17]), .in18(in_1[18]),
    .in19(in_1[19]), .in20(in_1[20]), .in21(in_1[21]), .in22(in_1[22]), .in23(in_1[23]), .in24(in_1[24]),
    .in25(in_1[25]), .in26(1'b0), .in27(1'b0), .in28(1'b0), .in29(1'b0), .in30(1'b0), .in31(1'b0),
    .out(out_2), .gs(priority_encoder_1_gs), .en_out(priority_encoder_1_en_out), .en_in(1'b1));
endmodule

module plugboard (
  input  [25:0] in_1,
  output [25:0] out_2,
  output [4:0] out_3
);

  encoder encoder_1 (.in_1(in_1), .out_2(out_3));

  assign out_2 = {in_1[12], in_1[0], in_1[7], in_1[16], in_1[1], in_1[18], in_1[13], in_1[17], in_1[8], in_1[24], in_1[21], in_1[14], in_1[5], in_1[25], in_1[10], in_1[6], in_1[9], in_1[22], in_1[23], in_1[3], in_1[4], in_1[19], in_1[20], in_1[15], in_1[2], in_1[11]};
endmodule

module reflector (
  input  [25:0] in_1,
  output [4:0] out_2,
  output [25:0] out_3
);

  wire clock_1_out;
  wire [4:0] encoder_1_out_2;

  encoder encoder_1 (.in_1(in_1), .out_2(encoder_1_out_2));
  Clock clock_1 (.out(clock_1_out));
  ROM #(.addrWidth(5), .dataWidth(5)) rom_1 (.addr(encoder_1_out_2), .data(out_2));  // open: sel
  decoder decoder_1 (.in_1(out_2), .out_2(out_3));

  // Notes on the sheet:
  //   contents of rom_1 (hex, n*v repeats v):
  //   1 3 5 4 9 8 7 a b 10 11
endmodule

module decoder (
  input  [4:0] in_1,
  output [25:0] out_2
);

  Demultiplexer #(.select(5)) demultiplexer_1 (
    .out0(out_2[0]), .out1(out_2[1]), .out2(out_2[2]), .out3(out_2[3]), .out4(out_2[4]), .out5(out_2[5]),
    .out6(out_2[6]), .out7(out_2[7]), .out8(out_2[8]), .out9(out_2[9]), .out10(out_2[10]), .out11(out_2[11]),
    .out12(out_2[12]), .out13(out_2[13]), .out14(out_2[14]), .out15(out_2[15]), .out16(out_2[16]),
    .out17(out_2[17]), .out18(out_2[18]), .out19(out_2[19]), .out20(out_2[20]), .out21(out_2[21]),
    .out22(out_2[22]), .out23(out_2[23]), .out24(out_2[24]), .out25(out_2[25]), .in(1'b1), .sel(in_1),
    .en(1'b1));  // open: out26, out27, out28, out29, out30, out31
endmodule

module switch (
  input  in_1,
  input  in_2,
  output out_3,
  output out_4
);

  Transistor transistor_1 (.in(in_2), .out(out_3), .gate(in_1));
  Transistor #(.\type ("n"), .gate("br")) transistor_2 (.in(1'b1), .out(out_4), .gate(in_1));
endmodule

module connector_in (
  input  in_1,
  input  in_2,
  input  in_3,
  input  in_4,
  input  in_5,
  input  in_6,
  input  in_7,
  input  in_8,
  input  in_9,
  input  [8:0] in_10,
  output out_11,
  output out_12,
  output out_13,
  output out_14,
  output out_15,
  output out_16,
  output out_17,
  output out_18,
  output out_19,
  output [8:0] out_20
);


  assign out_11 = in_10[0];
  assign out_12 = in_10[1];
  assign out_13 = in_10[2];
  assign out_14 = in_10[3];
  assign out_15 = in_10[4];
  assign out_16 = in_10[5];
  assign out_17 = in_10[6];
  assign out_18 = in_10[7];
  assign out_19 = in_10[8];
  assign out_20 = {in_9, in_8, in_7, in_6, in_5, in_4, in_3, in_2, in_1};
endmodule

module letter_converter (
  input  in_1,
  input  in_2,
  input  in_3,
  input  in_4,
  input  in_5,
  input  in_6,
  input  in_7,
  input  in_8,
  input  in_9,
  input  in_10,
  input  in_11,
  input  in_12,
  input  in_13,
  input  in_14,
  input  in_15,
  input  in_16,
  input  in_17,
  input  in_18,
  input  in_19,
  input  in_20,
  input  in_21,
  input  in_22,
  input  in_23,
  input  in_24,
  input  in_25,
  input  in_26,
  input  [25:0] in_27,
  output out_28,
  output out_29,
  output out_30,
  output out_31,
  output out_32,
  output out_33,
  output out_34,
  output out_35,
  output out_36,
  output out_37,
  output out_38,
  output out_39,
  output out_40,
  output out_41,
  output out_42,
  output out_43,
  output out_44,
  output out_45,
  output out_46,
  output out_47,
  output out_48,
  output out_49,
  output out_50,
  output out_51,
  output out_52,
  output out_53,
  output [25:0] out_54
);


  assign out_28 = in_27[0];
  assign out_29 = in_27[1];
  assign out_30 = in_27[2];
  assign out_31 = in_27[3];
  assign out_32 = in_27[4];
  assign out_33 = in_27[5];
  assign out_34 = in_27[6];
  assign out_35 = in_27[7];
  assign out_36 = in_27[8];
  assign out_37 = in_27[9];
  assign out_38 = in_27[10];
  assign out_39 = in_27[11];
  assign out_40 = in_27[12];
  assign out_41 = in_27[13];
  assign out_42 = in_27[14];
  assign out_43 = in_27[15];
  assign out_44 = in_27[16];
  assign out_45 = in_27[17];
  assign out_46 = in_27[18];
  assign out_47 = in_27[19];
  assign out_48 = in_27[20];
  assign out_49 = in_27[21];
  assign out_50 = in_27[22];
  assign out_51 = in_27[23];
  assign out_52 = in_27[24];
  assign out_53 = in_27[25];
  assign out_54 = {in_26, in_25, in_24, in_23, in_22, in_21, in_20, in_19, in_18, in_17, in_16, in_15, in_14, in_13, in_12, in_11, in_10, in_9, in_8, in_7, in_6, in_5, in_4, in_3, in_2, in_1};
endmodule

module connector_out (
  input  [8:0] in_1,
  output out_2,
  output out_3,
  output out_4,
  output out_5,
  output out_6,
  output out_7,
  output out_8,
  output out_9,
  output out_10
);


  assign out_2 = in_1[8];
  assign out_3 = in_1[7];
  assign out_4 = in_1[6];
  assign out_5 = in_1[5];
  assign out_6 = in_1[4];
  assign out_7 = in_1[3];
  assign out_8 = in_1[2];
  assign out_9 = in_1[1];
  assign out_10 = in_1[0];
endmodule
