// Logisim project enigma.circ as structural Verilog: 13 circuits, main circuit main
module main (
);

  wire A_out, B_out, buffer_1_out, button_1_out, C_out, clock_1_out, connector_in_1_out_11,
       connector_in_1_out_12, connector_in_1_out_13, connector_in_1_out_14, connector_in_1_out_15,
       connector_in_1_out_16, connector_in_1_out_17, connector_in_1_out_18, connector_in_1_out_19,
       connector_in_2_out_11, connector_in_2_out_12, connector_in_2_out_13, connector_in_2_out_14,
       connector_in_2_out_15, connector_in_2_out_16, connector_in_2_out_17, connector_in_2_out_18,
       connector_in_3_out_11, connector_in_3_out_12, connector_in_3_out_13, connector_in_3_out_14,
       connector_in_3_out_15, connector_in_3_out_16, connector_in_3_out_17, connector_in_3_out_18,
       connector_in_3_out_19, D_out, E_out, F_out, G_out, H_out, I_out, J_out, K_out, L_out,
       letter_converter_1_out_28, letter_converter_1_out_29, letter_converter_1_out_30,
       letter_converter_1_out_31, letter_converter_1_out_33, letter_converter_1_out_34,
       letter_converter_1_out_35, letter_converter_1_out_37, letter_converter_1_out_38,
       letter_converter_1_out_39, letter_converter_1_out_40, letter_converter_1_out_41,
       letter_converter_1_out_43, letter_converter_1_out_46, letter_converter_1_out_49,
       letter_converter_1_out_51, letter_converter_1_out_52, letter_converter_2_out_29,
       letter_converter_2_out_30, letter_converter_2_out_32, letter_converter_2_out_36,
       letter_converter_2_out_39, letter_converter_2_out_40, letter_converter_2_out_41,
       letter_converter_2_out_42, letter_converter_2_out_43, letter_converter_2_out_44,
       letter_converter_2_out_45, letter_converter_2_out_47, letter_converter_2_out_48,
       letter_converter_2_out_49, letter_converter_2_out_50, letter_converter_2_out_51,
       letter_converter_2_out_52, letter_converter_2_out_53, letter_converter_3_out_28,
       letter_converter_3_out_31, letter_converter_3_out_32, letter_converter_3_out_33,
       letter_converter_3_out_34, letter_converter_3_out_35, letter_converter_3_out_36,
       letter_converter_3_out_37, letter_converter_3_out_38, letter_converter_3_out_42,
       letter_converter_3_out_44, letter_converter_3_out_45, letter_converter_3_out_46,
       letter_converter_3_out_47, letter_converter_3_out_48, letter_converter_3_out_50,
       letter_converter_3_out_53, M_out, N_out, O_out, out_1_out_2, out_1_out_3, out_1_out_4, out_1_out_5,
       out_1_out_6, out_1_out_7, out_1_out_8, out_1_out_9, out_1_out_10, out_2_out_2, out_2_out_3,
       out_2_out_4, out_2_out_5, out_2_out_6, out_2_out_7, out_2_out_8, out_2_out_9, out_3_out_2,
       out_3_out_3, out_3_out_4, out_3_out_5, out_3_out_6, out_3_out_7, out_3_out_8, out_3_out_9,
       out_3_out_10, P_out, Q_out, R_out, reset_out, rotor_1_carry, S_out, switch_1_out_3, switch_1_out_4,
       switch_2_out_3, switch_2_out_4, switch_3_out_3, switch_3_out_4, switch_4_out_3, switch_4_out_4,
       switch_5_out_3, switch_5_out_4, switch_6_out_3, switch_6_out_4, switch_7_out_3, switch_7_out_4,
       switch_8_out_3, switch_8_out_4, switch_9_out_3, switch_9_out_4, switch_10_out_3, switch_10_out_4,
       switch_11_out_3, switch_11_out_4, switch_12_out_3, switch_12_out_4, switch_13_out_3, switch_13_out_4,
       switch_14_out_3, switch_14_out_4, switch_15_out_3, switch_15_out_4, switch_16_out_3, switch_16_out_4,
       switch_17_out_3, switch_17_out_4, switch_18_out_3, switch_18_out_4, switch_19_out_3, switch_19_out_4,
       switch_20_out_3, switch_20_out_4, switch_21_out_3, switch_21_out_4, switch_22_out_3, switch_22_out_4,
       switch_23_out_3, switch_23_out_4, switch_24_out_3, switch_24_out_4, switch_25_out_3, switch_25_out_4,
       switch_26_out_3, switch_26_out_4, T_out, U_out, undriven, undriven_2, undriven_3, undriven_4,
       undriven_5, undriven_6, undriven_7, undriven_8, undriven_9, undriven_10, undriven_11, undriven_12,
       undriven_13, undriven_14, undriven_15, undriven_16, undriven_17, undriven_18, undriven_19,
       undriven_20, undriven_21, undriven_22, undriven_23, undriven_24, undriven_25, undriven_26,
       undriven_27, undriven_28, undriven_29, undriven_30, undriven_31, undriven_32, undriven_33,
       undriven_34, undriven_35, undriven_36, undriven_37, undriven_38, undriven_39, undriven_40,
       undriven_41, undriven_42, undriven_43, undriven_44, undriven_45, undriven_46, undriven_47,
       undriven_48, undriven_49, undriven_50, undriven_51, undriven_52, V_out, W_out, X_out, Y_out, Z_out;
  wire [1:0] transistor_1_out;
  wire [1:1] test_1_out_3;
  wire [4:0] encoder_1_out_2, rotor_1_letters_in, rotor_1_pos_out;
  wire [8:0] connector_in_1_out_20, connector_in_2_out_20, connector_in_3_out_20, letter_converter_1_out_44,
       letter_converter_2_out_28, letter_converter_3_out_43, out1, out2, out3;
  wire [25:0] rotor_1_out_6;
  wire [25:6] letter_converter_1_out_54;

  Button button_1 (.out(button_1_out));
  Transistor #(.\type ("n")) transistor_1 (.in(1'b1), .out(transistor_1_out[0]), .gate(button_1_out));
  test test_1 (
    .in_1(transistor_1_out), .out_4(transistor_1_out), .out_3({2{test_1_out_3[1]}}),
    .in_2({2{test_1_out_3[1]}}));
  switch switch_1 (.in_1(Q_out), .in_2(connector_in_1_out_11), .out_3(switch_1_out_3), .out_4(switch_1_out_4));
  Button Q (.out(Q_out));
  connector_in connector_in_1 (
    .in_1(switch_1_out_4), .in_2(switch_6_out_4), .in_3(switch_5_out_4), .in_4(switch_12_out_4),
    .out_20(connector_in_1_out_20), .in_5(switch_11_out_4), .in_6(switch_17_out_4), .in_7(switch_18_out_4),
    .in_8(switch_24_out_4), .in_9(switch_23_out_4), .out_11(connector_in_1_out_11),
    .out_12(connector_in_1_out_12), .out_13(connector_in_1_out_13), .out_14(connector_in_1_out_14),
    .out_15(connector_in_1_out_15), .out_16(connector_in_1_out_16), .out_17(connector_in_1_out_17),
    .out_18(connector_in_1_out_18), .out_19(connector_in_1_out_19), .in_10(letter_converter_1_out_44));
  switch switch_2 (.in_1(A_out), .in_2(connector_in_2_out_11), .out_3(switch_2_out_3), .out_4(switch_2_out_4));
  Button A (.out(A_out));
  connector_in connector_in_2 (
    .in_1(switch_2_out_4), .in_2(switch_7_out_4), .in_3(switch_8_out_4), .in_4(switch_14_out_4),
    .out_20(connector_in_2_out_20), .in_5(switch_13_out_4), .in_6(switch_19_out_4), .in_7(switch_20_out_4),
    .in_8(switch_25_out_4), .out_11(connector_in_2_out_11), .out_12(connector_in_2_out_12),
    .out_13(connector_in_2_out_13), .out_14(connector_in_2_out_14), .out_15(connector_in_2_out_15),
    .out_16(connector_in_2_out_16), .out_17(connector_in_2_out_17), .out_18(connector_in_2_out_18),
    .in_10(letter_converter_2_out_28));  // open: in_9, out_19
  switch switch_3 (.in_1(Y_out), .in_2(connector_in_3_out_12), .out_3(switch_3_out_3), .out_4(switch_3_out_4));
  switch switch_4 (.in_1(P_out), .in_2(connector_in_3_out_11), .out_3(switch_4_out_3), .out_4(switch_4_out_4));
  Button P (.out(P_out));
  Button Y (.out(Y_out));
  connector_in connector_in_3 (
    .in_1(switch_4_out_4), .in_2(switch_3_out_4), .in_3(switch_10_out_4), .in_4(switch_9_out_4),
    .out_20(connector_in_3_out_20), .in_5(switch_16_out_4), .in_6(switch_15_out_4), .in_7(switch_21_out_4),
    .in_8(switch_22_out_4), .in_9(switch_26_out_4), .out_11(connector_in_3_out_11),
    .out_12(connector_in_3_out_12), .out_13(connector_in_3_out_13), .out_14(connector_in_3_out_14),
    .out_15(connector_in_3_out_15), .out_16(connector_in_3_out_16), .out_17(connector_in_3_out_17),
    .out_18(connector_in_3_out_18), .out_19(connector_in_3_out_19), .in_10(letter_converter_3_out_43));
  letters_display letters_display_1 ();  // open: out_1
  Button W (.out(W_out));
  Button E (.out(E_out));
  switch switch_5 (.in_1(E_out), .in_2(connector_in_1_out_13), .out_3(switch_5_out_3), .out_4(switch_5_out_4));
  switch switch_6 (.in_1(W_out), .in_2(connector_in_1_out_12), .out_3(switch_6_out_3), .out_4(switch_6_out_4));
  switch switch_7 (.in_1(S_out), .in_2(connector_in_2_out_12), .out_3(switch_7_out_3), .out_4(switch_7_out_4));
  Button S (.out(S_out));
  Button D (.out(D_out));
  switch switch_8 (.in_1(D_out), .in_2(connector_in_2_out_13), .out_3(switch_8_out_3), .out_4(switch_8_out_4));
  Button X (.out(X_out));
  Button C (.out(C_out));
  switch switch_9 (.in_1(C_out), .in_2(connector_in_3_out_14), .out_3(switch_9_out_3), .out_4(switch_9_out_4));
  switch switch_10 (.in_1(X_out), .in_2(connector_in_3_out_13), .out_3(switch_10_out_3), .out_4(switch_10_out_4));
  Button T (.out(T_out));
  switch switch_11 (.in_1(T_out), .in_2(connector_in_1_out_15), .out_3(switch_11_out_3), .out_4(switch_11_out_4));
  Button R (.out(R_out));
  switch switch_12 (.in_1(R_out), .in_2(connector_in_1_out_14), .out_3(switch_12_out_3), .out_4(switch_12_out_4));
  Button G (.out(G_out));
  switch switch_13 (.in_1(G_out), .in_2(connector_in_2_out_15), .out_3(switch_13_out_3), .out_4(switch_13_out_4));
  Button F (.out(F_out));
  switch switch_14 (.in_1(F_out), .in_2(connector_in_2_out_14), .out_3(switch_14_out_3), .out_4(switch_14_out_4));
  switch switch_15 (.in_1(B_out), .in_2(connector_in_3_out_16), .out_3(switch_15_out_3), .out_4(switch_15_out_4));
  Button V (.out(V_out));
  switch switch_16 (.in_1(V_out), .in_2(connector_in_3_out_15), .out_3(switch_16_out_3), .out_4(switch_16_out_4));
  Button B (.out(B_out));
  switch switch_17 (.in_1(Z_out), .in_2(connector_in_1_out_16), .out_3(switch_17_out_3), .out_4(switch_17_out_4));
  Button U (.out(U_out));
  Button Z (.out(Z_out));
  switch switch_18 (.in_1(U_out), .in_2(connector_in_1_out_17), .out_3(switch_18_out_3), .out_4(switch_18_out_4));
  Button J (.out(J_out));
  switch switch_19 (.in_1(H_out), .in_2(connector_in_2_out_16), .out_3(switch_19_out_3), .out_4(switch_19_out_4));
  Button H (.out(H_out));
  switch switch_20 (.in_1(J_out), .in_2(connector_in_2_out_17), .out_3(switch_20_out_3), .out_4(switch_20_out_4));
  Button N (.out(N_out));
  switch switch_21 (.in_1(N_out), .in_2(connector_in_3_out_17), .out_3(switch_21_out_3), .out_4(switch_21_out_4));
  Button M (.out(M_out));
  switch switch_22 (.in_1(M_out), .in_2(connector_in_3_out_18), .out_3(switch_22_out_3), .out_4(switch_22_out_4));
  connector_in connector_in_4 (
    .in_1(switch_23_out_3), .in_2(switch_24_out_3), .in_3(switch_18_out_3), .in_4(switch_17_out_3),
    .out_20(out1), .in_5(switch_11_out_3), .in_6(switch_12_out_3), .in_7(switch_5_out_3),
    .in_8(switch_6_out_3), .in_9(switch_1_out_3));  // open: out_11, out_12, out_13, out_14, out_15, out_16, out_17, out_18, out_19, in_10
  switch switch_23 (.in_1(O_out), .in_2(connector_in_1_out_19), .out_3(switch_23_out_3), .out_4(switch_23_out_4));
  Button O (.out(O_out));
  switch switch_24 (.in_1(I_out), .in_2(connector_in_1_out_18), .out_3(switch_24_out_3), .out_4(switch_24_out_4));
  Button I (.out(I_out));
  letter_converter letter_converter_1 (
    .in_1(undriven_51), .in_2(undriven_50), .in_3(undriven_47), .in_4(undriven_44),
    .in_5(connector_in_1_out_20[2]), .in_6(undriven_40), .in_7(undriven_38), .in_8(undriven_36),
    .in_9(connector_in_1_out_20[7]), .in_10(undriven_32), .in_11(undriven_31), .in_12(undriven_30),
    .in_13(undriven_28), .in_14(undriven_25), .in_15(connector_in_1_out_20[8]), .in_16(undriven_21),
    .in_17(connector_in_1_out_20[0]), .in_18(connector_in_1_out_20[3]), .in_19(undriven_14),
    .in_20(connector_in_1_out_20[4]), .in_21(connector_in_1_out_20[6]), .in_22(undriven_9),
    .in_23(connector_in_1_out_20[1]), .in_24(undriven_6), .in_25(undriven_3),
    .in_26(connector_in_1_out_20[5]),
    .out_54({letter_converter_1_out_54[25:23], letter_converter_1_out_54[24:23], letter_converter_1_out_54[20:18], letter_converter_1_out_54[19], letter_converter_1_out_54[16], letter_converter_1_out_54[25], letter_converter_1_out_54[14], letter_converter_1_out_54[16], letter_converter_1_out_54[12], letter_converter_1_out_54[20], letter_converter_1_out_54[10:8], letter_converter_1_out_54[9], {2{letter_converter_1_out_54[6]}}, letter_converter_1_out_54[8], letter_converter_1_out_54[18], letter_converter_1_out_54[12], letter_converter_1_out_54[10], letter_converter_1_out_54[14]}),
    .out_28(letter_converter_1_out_28), .out_29(letter_converter_1_out_29),
    .out_30(letter_converter_1_out_30), .out_31(letter_converter_1_out_31),
    .out_32(letter_converter_1_out_44[2]), .out_33(letter_converter_1_out_33),
    .out_34(letter_converter_1_out_34), .out_35(letter_converter_1_out_35),
    .out_36(letter_converter_1_out_44[7]), .out_37(letter_converter_1_out_37),
    .out_38(letter_converter_1_out_38), .out_39(letter_converter_1_out_39),
    .out_40(letter_converter_1_out_40), .out_41(letter_converter_1_out_41),
    .out_42(letter_converter_1_out_44[8]), .out_43(letter_converter_1_out_43),
    .out_44(letter_converter_1_out_44[0]), .out_45(letter_converter_1_out_44[3]),
    .out_46(letter_converter_1_out_46), .out_47(letter_converter_1_out_44[4]),
    .out_48(letter_converter_1_out_44[6]), .out_49(letter_converter_1_out_49),
    .out_50(letter_converter_1_out_44[1]), .out_51(letter_converter_1_out_51),
    .out_52(letter_converter_1_out_52), .out_53(letter_converter_1_out_44[5]),
    .in_27({letter_converter_1_out_54[25:23], letter_converter_1_out_54[24:23], letter_converter_1_out_54[20:18], letter_converter_1_out_54[19], letter_converter_1_out_54[16], letter_converter_1_out_54[25], letter_converter_1_out_54[14], letter_converter_1_out_54[16], letter_converter_1_out_54[12], letter_converter_1_out_54[20], letter_converter_1_out_54[10:8], letter_converter_1_out_54[9], {2{letter_converter_1_out_54[6]}}, letter_converter_1_out_54[8], letter_converter_1_out_54[18], letter_converter_1_out_54[12], letter_converter_1_out_54[10], letter_converter_1_out_54[14]}));
  connector_in connector_in_5 (
    .in_2(switch_25_out_3), .in_3(switch_20_out_3), .in_4(switch_19_out_3), .out_20(out2),
    .in_5(switch_13_out_3), .in_6(switch_14_out_3), .in_7(switch_8_out_3), .in_8(switch_7_out_3),
    .in_9(switch_2_out_3));  // open: in_1, out_11, out_12, out_13, out_14, out_15, out_16, out_17, out_18, out_19, in_10
  switch switch_25 (.in_1(K_out), .in_2(connector_in_2_out_18), .out_3(switch_25_out_3), .out_4(switch_25_out_4));
  Button K (.out(K_out));
  letter_converter letter_converter_2 (
    .in_1(connector_in_2_out_20[0]), .in_2(undriven_48), .in_3(undriven_45), .in_4(connector_in_2_out_20[2]),
    .in_5(undriven_41), .in_6(connector_in_2_out_20[3]), .in_7(connector_in_2_out_20[4]),
    .in_8(connector_in_2_out_20[5]), .in_9(undriven_33), .in_10(connector_in_2_out_20[6]),
    .in_11(connector_in_2_out_20[7]), .in_12(undriven_29), .in_13(undriven_26), .in_14(undriven_24),
    .in_15(undriven_22), .in_16(undriven_19), .in_17(undriven_17), .in_18(undriven_15),
    .in_19(connector_in_2_out_20[1]), .in_20(undriven_12), .in_21(undriven_10), .in_22(undriven_8),
    .in_23(undriven_7), .in_24(undriven_4), .in_25(undriven_2), .in_26(undriven),
    .out_54({letter_converter_1_out_54[25:23], letter_converter_1_out_54[24:23], letter_converter_1_out_54[20:18], letter_converter_1_out_54[19], letter_converter_1_out_54[16], letter_converter_1_out_54[25], letter_converter_1_out_54[14], letter_converter_1_out_54[16], letter_converter_1_out_54[12], letter_converter_1_out_54[20], letter_converter_1_out_54[10:8], letter_converter_1_out_54[9], {2{letter_converter_1_out_54[6]}}, letter_converter_1_out_54[8], letter_converter_1_out_54[18], letter_converter_1_out_54[12], letter_converter_1_out_54[10], letter_converter_1_out_54[14]}),
    .out_28(letter_converter_2_out_28[0]), .out_29(letter_converter_2_out_29),
    .out_30(letter_converter_2_out_30), .out_31(letter_converter_2_out_28[2]),
    .out_32(letter_converter_2_out_32), .out_33(letter_converter_2_out_28[3]),
    .out_34(letter_converter_2_out_28[4]), .out_35(letter_converter_2_out_28[5]),
    .out_36(letter_converter_2_out_36), .out_37(letter_converter_2_out_28[6]),
    .out_38(letter_converter_2_out_28[7]), .out_39(letter_converter_2_out_39),
    .out_40(letter_converter_2_out_40), .out_41(letter_converter_2_out_41),
    .out_42(letter_converter_2_out_42), .out_43(letter_converter_2_out_43),
    .out_44(letter_converter_2_out_44), .out_45(letter_converter_2_out_45),
    .out_46(letter_converter_2_out_28[1]), .out_47(letter_converter_2_out_47),
    .out_48(letter_converter_2_out_48), .out_49(letter_converter_2_out_49),
    .out_50(letter_converter_2_out_50), .out_51(letter_converter_2_out_51),
    .out_52(letter_converter_2_out_52), .out_53(letter_converter_2_out_53),
    .in_27({letter_converter_1_out_54[25:23], letter_converter_1_out_54[24:23], letter_converter_1_out_54[20:18], letter_converter_1_out_54[19], letter_converter_1_out_54[16], letter_converter_1_out_54[25], letter_converter_1_out_54[14], letter_converter_1_out_54[16], letter_converter_1_out_54[12], letter_converter_1_out_54[20], letter_converter_1_out_54[10:8], letter_converter_1_out_54[9], {2{letter_converter_1_out_54[6]}}, letter_converter_1_out_54[8], letter_converter_1_out_54[18], letter_converter_1_out_54[12], letter_converter_1_out_54[10], letter_converter_1_out_54[14]}));
  connector_in connector_in_6 (
    .in_1(switch_26_out_3), .in_2(switch_22_out_3), .in_3(switch_21_out_3), .in_4(switch_15_out_3),
    .out_20(out3), .in_5(switch_16_out_3), .in_6(switch_9_out_3), .in_7(switch_10_out_3),
    .in_8(switch_3_out_3), .in_9(switch_4_out_3));  // open: out_11, out_12, out_13, out_14, out_15, out_16, out_17, out_18, out_19, in_10
  Button L (.out(L_out));
  switch switch_26 (.in_1(L_out), .in_2(connector_in_3_out_19), .out_3(switch_26_out_3), .out_4(switch_26_out_4));
  letter_converter letter_converter_3 (
    .in_1(undriven_52), .in_2(connector_in_3_out_20[5]), .in_3(connector_in_3_out_20[3]), .in_4(undriven_49),
    .in_5(undriven_46), .in_6(undriven_43), .in_7(undriven_42), .in_8(undriven_39), .in_9(undriven_37),
    .in_10(undriven_35), .in_11(undriven_34), .in_12(connector_in_3_out_20[8]),
    .in_13(connector_in_3_out_20[7]), .in_14(connector_in_3_out_20[6]), .in_15(undriven_27),
    .in_16(connector_in_3_out_20[0]), .in_17(undriven_23), .in_18(undriven_20), .in_19(undriven_18),
    .in_20(undriven_16), .in_21(undriven_13), .in_22(connector_in_3_out_20[4]), .in_23(undriven_11),
    .in_24(connector_in_3_out_20[2]), .in_25(connector_in_3_out_20[1]), .in_26(undriven_5),
    .out_54({letter_converter_1_out_54[25:23], letter_converter_1_out_54[24:23], letter_converter_1_out_54[20:18], letter_converter_1_out_54[19], letter_converter_1_out_54[16], letter_converter_1_out_54[25], letter_converter_1_out_54[14], letter_converter_1_out_54[16], letter_converter_1_out_54[12], letter_converter_1_out_54[20], letter_converter_1_out_54[10:8], letter_converter_1_out_54[9], {2{letter_converter_1_out_54[6]}}, letter_converter_1_out_54[8], letter_converter_1_out_54[18], letter_converter_1_out_54[12], letter_converter_1_out_54[10], letter_converter_1_out_54[14]}),
    .out_28(letter_converter_3_out_28), .out_29(letter_converter_3_out_43[5]),
    .out_30(letter_converter_3_out_43[3]), .out_31(letter_converter_3_out_31),
    .out_32(letter_converter_3_out_32), .out_33(letter_converter_3_out_33),
    .out_34(letter_converter_3_out_34), .out_35(letter_converter_3_out_35),
    .out_36(letter_converter_3_out_36), .out_37(letter_converter_3_out_37),
    .out_38(letter_converter_3_out_38), .out_39(letter_converter_3_out_43[8]),
    .out_40(letter_converter_3_out_43[7]), .out_41(letter_converter_3_out_43[6]),
    .out_42(letter_converter_3_out_42), .out_43(letter_converter_3_out_43[0]),
    .out_44(letter_converter_3_out_44), .out_45(letter_converter_3_out_45),
    .out_46(letter_converter_3_out_46), .out_47(letter_converter_3_out_47),
    .out_48(letter_converter_3_out_48), .out_49(letter_converter_3_out_43[4]),
    .out_50(letter_converter_3_out_50), .out_51(letter_converter_3_out_43[2]),
    .out_52(letter_converter_3_out_43[1]), .out_53(letter_converter_3_out_53),
    .in_27({letter_converter_1_out_54[25:23], letter_converter_1_out_54[24:23], letter_converter_1_out_54[20:18], letter_converter_1_out_54[19], letter_converter_1_out_54[16], letter_converter_1_out_54[25], letter_converter_1_out_54[14], letter_converter_1_out_54[16], letter_converter_1_out_54[12], letter_converter_1_out_54[20], letter_converter_1_out_54[10:8], letter_converter_1_out_54[9], {2{letter_converter_1_out_54[6]}}, letter_converter_1_out_54[8], letter_converter_1_out_54[18], letter_converter_1_out_54[12], letter_converter_1_out_54[10], letter_converter_1_out_54[14]}));
  Clock clock_1 (.out(clock_1_out));
  letters_display letters_display_2 ();  // open: out_1
  connector_out out_3 (
    .out_2(out_3_out_2), .out_3(out_3_out_3), .out_4(out_3_out_4), .out_5(out_3_out_5), .out_6(out_3_out_6),
    .out_7(out_3_out_7), .out_8(out_3_out_8), .out_9(out_3_out_9), .out_10(out_3_out_10), .in_1(out3));
  connector_out out_1 (
    .out_2(out_1_out_2), .out_3(out_1_out_3), .out_4(out_1_out_4), .out_5(out_1_out_5), .out_6(out_1_out_6),
    .out_7(out_1_out_7), .out_8(out_1_out_8), .out_9(out_1_out_9), .out_10(out_1_out_10), .in_1(out1));
  LED E_2 (.in(out_1_out_4));
  LED W_2 (.in(out_1_out_3));
  LED Q_2 (.in(out_1_out_2));
  connector_out out_2 (
    .out_2(out_2_out_2), .out_3(out_2_out_3), .out_4(out_2_out_4), .out_5(out_2_out_5), .out_6(out_2_out_6),
    .out_7(out_2_out_7), .out_8(out_2_out_8), .out_9(out_2_out_9), .in_1(out2));  // open: out_10
  LED S_2 (.in(out_2_out_3));
  LED A_2 (.in(out_2_out_2));
  LED X_2 (.in(out_3_out_4));
  LED Y_2 (.in(out_3_out_3));
  LED P_2 (.in(out_3_out_2));
  buf buffer_1 (buffer_1_out, out1[8]);
  // Probe on encoder_1_out_2
  encoder encoder_1 (
    .in_1({letter_converter_1_out_54[25], letter_converter_1_out_54[9], {2{letter_converter_1_out_54[24]}}, {2{letter_converter_1_out_54[23]}}, letter_converter_1_out_54[19:18], letter_converter_1_out_54[19], letter_converter_1_out_54[16], letter_converter_1_out_54[25], letter_converter_1_out_54[14], letter_converter_1_out_54[16], letter_converter_1_out_54[12], {2{letter_converter_1_out_54[10]}}, letter_converter_1_out_54[9], letter_converter_1_out_54[20], letter_converter_1_out_54[8], {2{letter_converter_1_out_54[6]}}, letter_converter_1_out_54[12], letter_converter_1_out_54[18], letter_converter_1_out_54[14], letter_converter_1_out_54[20], letter_converter_1_out_54[8]}),
    .out_2(encoder_1_out_2));
  LED T_2 (.in(out_1_out_6));
  LED R_2 (.in(out_1_out_5));
  LED G_2 (.in(out_2_out_6));
  LED D_2 (.in(out_2_out_4));
  LED F_2 (.in(out_2_out_5));
  LED B_2 (.in(out_3_out_7));
  LED V_2 (.in(out_3_out_6));
  LED C_2 (.in(out_3_out_5));
  buf buffer_2 (buffer_1_out, out1[5]);
  buf buffer_3 (buffer_1_out, out1[7]);
  buf buffer_4 (buffer_1_out, out1[0]);
  buf buffer_5 (buffer_1_out, out1[2]);
  buf buffer_6 (buffer_1_out, out1[3]);
  buf buffer_7 (buffer_1_out, out1[6]);
  buf buffer_8 (buffer_1_out, out1[1]);
  buf buffer_9 (buffer_1_out, out1[4]);
  rotor rotor_1 (
    .out_6(rotor_1_out_6),
    .letters({letter_converter_1_out_54[25], letter_converter_1_out_54[9], {2{letter_converter_1_out_54[24]}}, {2{letter_converter_1_out_54[23]}}, letter_converter_1_out_54[19:18], letter_converter_1_out_54[19], letter_converter_1_out_54[16], letter_converter_1_out_54[25], letter_converter_1_out_54[14], letter_converter_1_out_54[16], letter_converter_1_out_54[12], {2{letter_converter_1_out_54[10]}}, letter_converter_1_out_54[9], letter_converter_1_out_54[20], letter_converter_1_out_54[8], {2{letter_converter_1_out_54[6]}}, letter_converter_1_out_54[12], letter_converter_1_out_54[18], letter_converter_1_out_54[14], letter_converter_1_out_54[20], letter_converter_1_out_54[8]}),
    .pos_in(5'b00001), .increment(buffer_1_out), .pos_out(rotor_1_pos_out), .set(reset_out),
    .carry(rotor_1_carry), .letters_in(rotor_1_letters_in));
  // Probe on rotor_1_letters_in
  // Probe on rotor_1_pos_out
  LED U_2 (.in(out_1_out_8));
  LED I_2 (.in(out_1_out_9));
  LED Z_2 (.in(out_1_out_7));
  LED H_2 (.in(out_2_out_7));
  LED J_2 (.in(out_2_out_8));
  LED K_2 (.in(out_2_out_9));
  LED N_2 (.in(out_3_out_8));
  LED M_2 (.in(out_3_out_9));
  buf buffer_10 (buffer_1_out, out2[8]);
  buf buffer_11 (buffer_1_out, out2[1]);
  buf buffer_12 (buffer_1_out, out2[2]);
  buf buffer_13 (buffer_1_out, out2[3]);
  buf buffer_14 (buffer_1_out, out2[4]);
  buf buffer_15 (buffer_1_out, out2[5]);
  buf buffer_16 (buffer_1_out, out2[7]);
  buf buffer_17 (buffer_1_out, out2[6]);
  Pull_Resistor pull_resistor_1 (.node(buffer_1_out));
  Button reset (.out(reset_out));
  // Probe on rotor_1_carry
  LED O_2 (.in(out_1_out_10));
  LED L_2 (.in(out_3_out_10));
  buf buffer_18 (buffer_1_out, out3[5]);
  buf buffer_19 (buffer_1_out, out3[7]);
  buf buffer_20 (buffer_1_out, out2[0]);
  buf buffer_21 (buffer_1_out, out3[6]);
  buf buffer_22 (buffer_1_out, out3[8]);
  buf buffer_23 (buffer_1_out, out3[2]);
  buf buffer_24 (buffer_1_out, out3[3]);
  buf buffer_25 (buffer_1_out, out3[4]);
  buf buffer_26 (buffer_1_out, out3[0]);
  buf buffer_27 (buffer_1_out, out3[1]);

  // Notes on the sheet:
  //   Plugboard
  //   Enigma
  //   Reflector
endmodule

module rotor (
  input  [25:0] letters,
  input  set,
  input  increment,
  input  [4:0] pos_in,
  output [4:0] letters_in,
  output [25:0] out_6,
  output [4:0] pos_out,
  output carry
);

  wire and_1_out, and_2_out, clock_1_out, d_ff_1_qn, demultiplexer_1_out0, demultiplexer_1_out1,
       demultiplexer_1_out2, demultiplexer_1_out3, demultiplexer_1_out4, demultiplexer_1_out5,
       demultiplexer_1_out6, demultiplexer_1_out7, demultiplexer_1_out8, demultiplexer_1_out9,
       demultiplexer_1_out10, demultiplexer_1_out11, demultiplexer_1_out12, demultiplexer_1_out13,
       demultiplexer_1_out14, demultiplexer_1_out15, demultiplexer_1_out16, demultiplexer_1_out17,
       demultiplexer_1_out18, demultiplexer_1_out19, demultiplexer_1_out20, demultiplexer_1_out21,
       demultiplexer_1_out22, demultiplexer_1_out23, demultiplexer_1_out24, demultiplexer_1_out25, not_1_out,
       push;
  wire [4:0] adder_out_3;

  Button button_1 ();  // open: out
  and and_1 (and_1_out, increment, not_1_out);
  not not_1 (not_1_out, set);
  encoder encoder_1 (.in_1(letters), .out_2(letters_in));
  or or_1 (push, set, increment);
  Counter #(.width(5), .max('h19)) counter_1 (
    .load(set), .D(pos_in), .count(and_1_out), .Q(pos_out), .carry(carry), .clk(and_2_out));  // open: clr
  and and_2 (and_2_out, clock_1_out, d_ff_1_qn);
  Clock clock_1 (.out(clock_1_out));
  // Probe on letters_in
  // Probe on pos_out
  // Probe on adder_out_3
  az_converter adder (.i1(letters_in), .i2(pos_out), .out_3(adder_out_3));
  // Probe on pos_out
  D_Flip_Flop d_ff_1 (.clk(clock_1_out), .D(and_1_out), .Qn(d_ff_1_qn));  // open: Q, preset, en, reset
  Demultiplexer #(.select(5)) demultiplexer_1 (
    .out0(demultiplexer_1_out0), .out1(demultiplexer_1_out1), .out2(demultiplexer_1_out2),
    .out3(demultiplexer_1_out3), .out4(demultiplexer_1_out4), .out5(demultiplexer_1_out5),
    .out6(demultiplexer_1_out6), .out7(demultiplexer_1_out7), .out8(demultiplexer_1_out8),
    .out9(demultiplexer_1_out9), .out10(demultiplexer_1_out10), .out11(demultiplexer_1_out11),
    .out12(demultiplexer_1_out12), .out13(demultiplexer_1_out13), .out14(demultiplexer_1_out14),
    .out15(demultiplexer_1_out15), .out16(demultiplexer_1_out16), .out17(demultiplexer_1_out17),
    .out18(demultiplexer_1_out18), .out19(demultiplexer_1_out19), .out20(demultiplexer_1_out20),
    .out21(demultiplexer_1_out21), .out22(demultiplexer_1_out22), .out23(demultiplexer_1_out23),
    .out24(demultiplexer_1_out24), .out25(demultiplexer_1_out25), .in(1'b1), .sel(adder_out_3), .en(1'b1));  // open: out26, out27, out28, out29, out30, out31
  Transistor #(.\type ("n")) transistor_1 (.in(demultiplexer_1_out0), .out(out_6[0]), .gate(demultiplexer_1_out0));
  Transistor #(.\type ("n")) transistor_2 (.in(demultiplexer_1_out1), .out(out_6[1]), .gate(demultiplexer_1_out1));
  Transistor #(.\type ("n")) transistor_3 (.in(demultiplexer_1_out2), .out(out_6[2]), .gate(demultiplexer_1_out2));
  Transistor #(.\type ("n")) transistor_4 (.in(demultiplexer_1_out3), .out(out_6[3]), .gate(demultiplexer_1_out3));
  Transistor #(.\type ("n")) transistor_5 (.in(demultiplexer_1_out4), .out(out_6[4]), .gate(demultiplexer_1_out4));
  Transistor #(.\type ("n")) transistor_6 (.in(demultiplexer_1_out5), .out(out_6[5]), .gate(demultiplexer_1_out5));
  Transistor #(.\type ("n")) transistor_7 (.in(demultiplexer_1_out6), .out(out_6[6]), .gate(demultiplexer_1_out6));
  Transistor #(.\type ("n")) transistor_8 (.in(demultiplexer_1_out7), .out(out_6[7]), .gate(demultiplexer_1_out7));
  Transistor #(.\type ("n")) transistor_9 (.in(demultiplexer_1_out8), .out(out_6[8]), .gate(demultiplexer_1_out8));
  Transistor #(.\type ("n")) transistor_10 (.in(demultiplexer_1_out9), .out(out_6[9]), .gate(demultiplexer_1_out9));
  Transistor #(.\type ("n")) transistor_11 (.in(demultiplexer_1_out10), .out(out_6[10]), .gate(demultiplexer_1_out10));
  Transistor #(.\type ("n")) transistor_12 (.in(demultiplexer_1_out11), .out(out_6[11]), .gate(demultiplexer_1_out11));
  Transistor #(.\type ("n")) transistor_13 (.in(demultiplexer_1_out12), .out(out_6[12]), .gate(demultiplexer_1_out12));
  Transistor #(.\type ("n")) transistor_14 (.in(demultiplexer_1_out13), .out(out_6[13]), .gate(demultiplexer_1_out13));
  Transistor #(.\type ("n")) transistor_15 (.in(demultiplexer_1_out14), .out(out_6[14]), .gate(demultiplexer_1_out14));
  Transistor #(.\type ("n")) transistor_16 (.in(demultiplexer_1_out15), .out(out_6[15]), .gate(demultiplexer_1_out15));
  Transistor #(.\type ("n")) transistor_17 (.in(demultiplexer_1_out16), .out(out_6[16]), .gate(demultiplexer_1_out16));
  Transistor #(.\type ("n")) transistor_18 (.in(demultiplexer_1_out17), .out(out_6[17]), .gate(demultiplexer_1_out17));
  Transistor #(.\type ("n")) transistor_19 (.in(demultiplexer_1_out18), .out(out_6[18]), .gate(demultiplexer_1_out18));
  Transistor #(.\type ("n")) transistor_20 (.in(demultiplexer_1_out19), .out(out_6[19]), .gate(demultiplexer_1_out19));
  Transistor #(.\type ("n")) transistor_21 (.in(demultiplexer_1_out20), .out(out_6[20]), .gate(demultiplexer_1_out20));
  Transistor #(.\type ("n")) transistor_22 (.in(demultiplexer_1_out21), .out(out_6[21]), .gate(demultiplexer_1_out21));
  Transistor #(.\type ("n")) transistor_23 (.in(demultiplexer_1_out22), .out(out_6[22]), .gate(demultiplexer_1_out22));
  Transistor #(.\type ("n")) transistor_24 (.in(demultiplexer_1_out23), .out(out_6[23]), .gate(demultiplexer_1_out23));
  Transistor #(.\type ("n")) transistor_25 (.in(demultiplexer_1_out24), .out(out_6[24]), .gate(demultiplexer_1_out24));
  Transistor #(.\type ("n")) transistor_26 (.in(demultiplexer_1_out25), .out(out_6[25]), .gate(demultiplexer_1_out25));
endmodule

module encoder (
  input  [25:0] in_1,
  output [4:0] out_2
);

  wire priority_encoder_1_en_out;

  Pull_Resistor pull_resistor_1 (.node(in_1[0]));
  Pull_Resistor pull_resistor_2 (.node(in_1[3]));
  Pull_Resistor pull_resistor_3 (.node(in_1[4]));
  Pull_Resistor pull_resistor_4 (.node(in_1[1]));
  Pull_Resistor pull_resistor_5 (.node(in_1[2]));
  Pull_Resistor pull_resistor_6 (.node(in_1[5]));
  Pull_Resistor pull_resistor_7 (.node(in_1[8]));
  Pull_Resistor pull_resistor_8 (.node(in_1[6]));
  Pull_Resistor pull_resistor_9 (.node(in_1[7]));
  Pull_Resistor pull_resistor_10 (.node(in_1[11]));
  Pull_Resistor pull_resistor_11 (.node(in_1[12]));
  Pull_Resistor pull_resistor_12 (.node(in_1[10]));
  Pull_Resistor pull_resistor_13 (.node(in_1[9]));
  Pull_Resistor pull_resistor_14 (.node(in_1[15]));
  Pull_Resistor pull_resistor_15 (.node(in_1[14]));
  Pull_Resistor pull_resistor_16 (.node(in_1[13]));
  Pull_Resistor pull_resistor_17 (.node(in_1[16]));
  Pull_Resistor pull_resistor_18 (.node(in_1[19]));
  Pull_Resistor pull_resistor_19 (.node(in_1[18]));
  Pull_Resistor pull_resistor_20 (.node(in_1[20]));
  Pull_Resistor pull_resistor_21 (.node(in_1[17]));
  Pull_Resistor pull_resistor_22 (.node(in_1[22]));
  Pull_Resistor pull_resistor_23 (.node(in_1[23]));
  Pull_Resistor pull_resistor_24 (.node(in_1[21]));
  Pull_Resistor pull_resistor_25 (.node(in_1[24]));
  Pull_Resistor pull_resistor_26 (.node(in_1[25]));
  // Probe on out_2
  Priority_Encoder #(.select(5)) priority_encoder_1 (
    .in0(in_1[0]), .in1(in_1[1]), .in2(in_1[2]), .in3(in_1[3]), .in4(in_1[4]), .in5(in_1[5]), .in6(in_1[6]),
    .in7(in_1[7]), .in8(in_1[8]), .in9(in_1[9]), .in10(in_1[10]), .in11(in_1[11]), .in12(in_1[12]),
    .in13(in_1[13]), .in14(in_1[14]), .in15(in_1[15]), .in16(in_1[16]), .in17(in_1[17]), .in18(in_1[18]),
    .in19(in_1[19]), .in20(in_1[20]), .in21(in_1[21]), .in22(in_1[22]), .in23(in_1[23]), .in24(in_1[24]),
    .in25(in_1[25]), .in26(1'b0), .in27(1'b0), .in28(1'b0), .in29(1'b0), .in30(1'b0), .in31(1'b0),
    .out(out_2), .en_out(priority_encoder_1_en_out), .en_in(1'b1));  // open: gs
endmodule

module plugboard (
  input  [25:0] in_1,
  output [25:0] out_2,
  output [4:0] out_3
);

  encoder encoder_1 (.in_1(in_1), .out_2(out_3));

  assign out_2 = {in_1[12], in_1[0], in_1[7], in_1[16], in_1[1], in_1[18], in_1[13], in_1[17], in_1[8], in_1[24], in_1[21], in_1[14], in_1[5], in_1[25], in_1[10], in_1[6], in_1[9], in_1[22], in_1[23], in_1[3], in_1[4], in_1[19], in_1[20], in_1[15], in_1[2], in_1[11]};
endmodule

module reflector (
  input  [25:0] in_1,
  output [4:0] out_2,
  output [25:0] out_3
);

  wire clock_1_out;
  wire [4:0] encoder_1_out_2;

  encoder encoder_1 (.in_1(in_1), .out_2(encoder_1_out_2));
  Clock clock_1 (.out(clock_1_out));
  ROM #(.addrWidth(5), .dataWidth(5)) rom_1 (.addr(encoder_1_out_2), .data(out_2));  // open: sel
  decoder decoder_1 (.in_1(out_2), .out_2(out_3));

  // Notes on the sheet:
  //   contents of rom_1 (hex, n*v repeats v):
  //   1 3 5 4 9 8 7 a b 10 11
endmodule

module decoder (
  input  [4:0] in_1,
  output [25:0] out_2
);

  Demultiplexer #(.select(5)) demultiplexer_1 (
    .out0(out_2[0]), .out1(out_2[1]), .out2(out_2[2]), .out3(out_2[3]), .out4(out_2[4]), .out5(out_2[5]),
    .out6(out_2[6]), .out7(out_2[7]), .out8(out_2[8]), .out9(out_2[9]), .out10(out_2[10]), .out11(out_2[11]),
    .out12(out_2[12]), .out13(out_2[13]), .out14(out_2[14]), .out15(out_2[15]), .out16(out_2[16]),
    .out17(out_2[17]), .out18(out_2[18]), .out19(out_2[19]), .out20(out_2[20]), .out21(out_2[21]),
    .out22(out_2[22]), .out23(out_2[23]), .out24(out_2[24]), .out25(out_2[25]), .in(1'b1), .sel(in_1),
    .en(1'b1));  // open: out26, out27, out28, out29, out30, out31
endmodule

module switch (
  input  in_1,
  input  in_2,
  output out_3,
  output out_4
);

  Transistor transistor_1 (.in(in_2), .out(out_3), .gate(in_1));
  Transistor #(.\type ("n"), .gate("br")) transistor_2 (.in(1'b1), .out(out_4), .gate(in_1));
endmodule

module connector_in (
  input  in_1,
  input  in_2,
  input  in_3,
  input  in_4,
  input  in_5,
  input  in_6,
  input  in_7,
  input  in_8,
  input  in_9,
  input  [8:0] in_10,
  output out_11,
  output out_12,
  output out_13,
  output out_14,
  output out_15,
  output out_16,
  output out_17,
  output out_18,
  output out_19,
  output [8:0] out_20
);


  assign out_11 = in_10[0];
  assign out_12 = in_10[1];
  assign out_13 = in_10[2];
  assign out_14 = in_10[3];
  assign out_15 = in_10[4];
  assign out_16 = in_10[5];
  assign out_17 = in_10[6];
  assign out_18 = in_10[7];
  assign out_19 = in_10[8];
  assign out_20 = {in_9, in_8, in_7, in_6, in_5, in_4, in_3, in_2, in_1};
endmodule

module connector_out (
  input  [8:0] in_1,
  output out_2,
  output out_3,
  output out_4,
  output out_5,
  output out_6,
  output out_7,
  output out_8,
  output out_9,
  output out_10
);


  assign out_2 = in_1[8];
  assign out_3 = in_1[7];
  assign out_4 = in_1[6];
  assign out_5 = in_1[5];
  assign out_6 = in_1[4];
  assign out_7 = in_1[3];
  assign out_8 = in_1[2];
  assign out_9 = in_1[1];
  assign out_10 = in_1[0];
endmodule

module letter_converter (
  input  in_1,
  input  in_2,
  input  in_3,
  input  in_4,
  input  in_5,
  input  in_6,
  input  in_7,
  input  in_8,
  input  in_9,
  input  in_10,
  input  in_11,
  input  in_12,
  input  in_13,
  input  in_14,
  input  in_15,
  input  in_16,
  input  in_17,
  input  in_18,
  input  in_19,
  input  in_20,
  input  in_21,
  input  in_22,
  input  in_23,
  input  in_24,
  input  in_25,
  input  in_26,
  input  [25:0] in_27,
  output out_28,
  output out_29,
  output out_30,
  output out_31,
  output out_32,
  output out_33,
  output out_34,
  output out_35,
  output out_36,
  output out_37,
  output out_38,
  output out_39,
  output out_40,
  output out_41,
  output out_42,
  output out_43,
  output out_44,
  output out_45,
  output out_46,
  output out_47,
  output out_48,
  output out_49,
  output out_50,
  output out_51,
  output out_52,
  output out_53,
  output [25:0] out_54
);


  assign out_28 = in_27[0];
  assign out_29 = in_27[1];
  assign out_30 = in_27[2];
  assign out_31 = in_27[3];
  assign out_32 = in_27[4];
  assign out_33 = in_27[5];
  assign out_34 = in_27[6];
  assign out_35 = in_27[7];
  assign out_36 = in_27[8];
  assign out_37 = in_27[9];
  assign out_38 = in_27[10];
  assign out_39 = in_27[11];
  assign out_40 = in_27[12];
  assign out_41 = in_27[13];
  assign out_42 = in_27[14];
  assign out_43 = in_27[15];
  assign out_44 = in_27[16];
  assign out_45 = in_27[17];
  assign out_46 = in_27[18];
  assign out_47 = in_27[19];
  assign out_48 = in_27[20];
  assign out_49 = in_27[21];
  assign out_50 = in_27[22];
  assign out_51 = in_27[23];
  assign out_52 = in_27[24];
  assign out_53 = in_27[25];
  assign out_54 = {in_26, in_25, in_24, in_23, in_22, in_21, in_20, in_19, in_18, in_17, in_16, in_15, in_14, in_13, in_12, in_11, in_10, in_9, in_8, in_7, in_6, in_5, in_4, in_3, in_2, in_1};
endmodule

module letters_display (
  output [25:0] out_1
);
endmodule

module az_converter (
  input  [4:0] i1,
  input  [4:0] i2,
  output [4:0] out_3
);

  wire comparator_1_lt, not_1_out;
  wire [4:0] adder_1_out, subtractor_1_out;

  // Probe on i1
  // Probe on i2
  Adder #(.width(5)) adder_1 (.a(i1), .b(i2), .out(adder_1_out));  // open: cin, cout
  // Probe on adder_1_out
  Comparator #(.width(5), .mode("unsigned")) comparator_1 (
    .a(adder_1_out), .b(5'b11010), .lt(comparator_1_lt));  // open: gt, eq
  not not_1 (not_1_out, comparator_1_lt);
  Subtractor #(.width(5)) subtractor_1 (.a(adder_1_out), .b(5'b11010), .out(subtractor_1_out));  // open: bin, bout
  // Probe on out_3
  assign out_3 = comparator_1_lt ? adder_1_out : 5'bz;  // Controlled_Buffer controlled_buffer_1
  assign out_3 = not_1_out ? subtractor_1_out : 5'bz;  // Controlled_Buffer controlled_buffer_2
endmodule

module test (
  input  [1:0] in_1,
  input  [1:0] in_2,
  output [1:0] out_3,
  output [1:0] out_4
);


  assign out_3 = {in_1[0], in_1[1]};
  assign out_4 = {in_2[0], in_2[1]};
endmodule
